// Logisim project 4_bit_adder.circ as structural Verilog: 1 circuit, main circuit main
module main (
  input  C_in,
  input  A0,
  input  B0,
  input  A1,
  input  B1,
  input  A2,
  input  B2,
  input  A3,
  input  B3,
  output C_out
);

  wire adder_1_cout, adder_2_cout, adder_3_cout, undriven;
  wire [3:0] adder_1_out;

  Adder #(.width(1)) adder_1 (.a(A0), .b(B0), .out(adder_1_out[0]), .cin(C_in), .cout(adder_1_cout));
  Adder #(.width(1)) adder_2 (.a(A1), .b(B1), .out(adder_1_out[1]), .cin(adder_1_cout), .cout(adder_2_cout));
  Adder #(.width(1)) adder_3 (.a(A2), .b(B2), .out(adder_1_out[2]), .cin(adder_2_cout), .cout(adder_3_cout));
  Adder #(.width(1)) adder_4 (.a(A3), .b(B3), .out(adder_1_out[3]), .cin(adder_3_cout), .cout(C_out));
  Hex_Digit_Display hex_digit_display_1 (.value(adder_1_out), .dp(undriven));
endmodule
