// Logisim project Circ1.circ as structural Verilog: 1 circuit, main circuit main
module main (
  input  X,
  input  Y,
  input  Z,
  output out_4
);

  wire and_1_out, and_2_out, and_3_out, not_1_out, not_2_out, or_1_out, or_2_out;

  or or_1 (or_1_out, X, Y);
  and and_1 (and_1_out, X, Y);
  not not_1 (not_1_out, and_1_out);
  and and_2 (and_2_out, or_1_out, not_1_out);
  or or_2 (or_2_out, and_2_out, Z);
  and and_3 (and_3_out, and_2_out, Z);
  not not_2 (not_2_out, and_3_out);
  and and_4 (out_4, or_2_out, not_2_out);
endmodule
